// Logisim project alu.circ as structural Verilog: 1 circuit, main circuit alu
module alu (
  input  [31:0] A,
  input  [31:0] B,
  input  [3:0] ALUSel,
  output [31:0] Result
);

  wire comparator_1_gt, comparator_2_gt, comparator_3_gt, comparator_4_gt, not_1_out, not_2_out, not_3_out;
  wire [31:0] add0, and1, bit_extender_1_out, bit_extender_2_out, bit_extender_3_out, or2, shifter_1_out,
       shifter_2_out, shifter_3_out, sll6, slt7, sra5, srl4, xor3;

  Adder #(.width(32)) adder_1 (.a(A), .b(B), .out(add0));  // open: cin, cout
  assign and1 = A & B;  // AND_Gate and_1, 32 bits wide
  assign or2 = A | B;  // OR_Gate or_1, 32 bits wide
  assign xor3 = A ^ B;  // XOR_Gate xor_1, 32 bits wide
  Multiplier #(.mode("twosComplement"), .width(32)) multiplier_1 ();  // open: a, b, out, cin, cout
  Multiplexer #(.enable("false"), .select(4), .width(32)) multiplexer_1 (
    .in0(add0), .in1(and1), .in2(or2), .in3(xor3), .in4(srl4), .in5(sra5), .in6(sll6), .in7(slt7),
    .out(Result), .sel(ALUSel));  // open: in8, in9, in10, in11, in12, in13, in14, in15
  Shifter #(.shift("lr"), .width(32)) shifter_1 (.in(A), .\dist (B[4:0]), .out(shifter_1_out));
  not not_1 (not_1_out, comparator_1_gt);
  Comparator #(.mode("unsigned"), .width(27)) comparator_1 (
    .a(B[31:5]), .b({27{1'b0}}), .gt(comparator_1_gt));  // open: eq, lt
  Shifter #(.shift("ar"), .width(32)) shifter_2 (.in(A), .\dist (B[4:0]), .out(shifter_2_out));
  not not_2 (not_2_out, comparator_2_gt);
  Comparator #(.mode("unsigned"), .width(27)) comparator_2 (
    .a(B[31:5]), .b({27{1'b0}}), .gt(comparator_2_gt));  // open: eq, lt
  Shifter #(.width(32)) shifter_3 (.in(A), .\dist (B[4:0]), .out(shifter_3_out));
  not not_3 (not_3_out, comparator_3_gt);
  Comparator #(.mode("unsigned"), .width(27)) comparator_3 (
    .a(B[31:5]), .b({27{1'b0}}), .gt(comparator_3_gt));  // open: eq, lt
  assign bit_extender_1_out = {{31{not_1_out}}, not_1_out};  // Bit_Extender bit_extender_1
  assign bit_extender_2_out = {{31{not_2_out}}, not_2_out};  // Bit_Extender bit_extender_2
  assign bit_extender_3_out = {{31{not_3_out}}, not_3_out};  // Bit_Extender bit_extender_3
  assign srl4 = shifter_1_out & bit_extender_1_out;  // AND_Gate and_2, 32 bits wide
  assign sra5 = shifter_2_out & bit_extender_2_out;  // AND_Gate and_3, 32 bits wide
  assign sll6 = shifter_3_out & bit_extender_3_out;  // AND_Gate and_4, 32 bits wide
  Comparator #(.width(32)) comparator_4 (.a(B), .b(A), .gt(comparator_4_gt));  // open: eq, lt
  assign slt7 = {{31{1'b0}}, comparator_4_gt};  // Bit_Extender bit_extender_4

  // Notes on the sheet:
  //   INPUTS to your circuit
  //   DON'T CHANGE THE LOCATIONS OF THE INPUTS AND OUTPUTS!
  //   OUTPUT from your circuit
endmodule
