// Logisim project branch_comp.circ as structural Verilog: 1 circuit, main circuit branch_comp
module branch_comp (
  input  [31:0] rs1,
  input  [31:0] rs2,
  input  BrUn,
  output BrEq,
  output BrLt
);

  wire signeq, signlt, unsigneq, unsignlt;

  Comparator #(.width(32)) comparator_1 (.a(rs1), .b(rs2), .eq(signeq), .lt(signlt));  // open: gt
  Comparator #(.mode("unsigned"), .width(32)) comparator_2 (
    .a(rs1), .b(rs2), .eq(unsigneq), .lt(unsignlt));  // open: gt
  Multiplexer #(.enable("false")) multiplexer_1 (.in0(signeq), .in1(unsigneq), .out(BrEq), .sel(BrUn));
  Multiplexer #(.enable("false")) multiplexer_2 (.in0(signlt), .in1(unsignlt), .out(BrLt), .sel(BrUn));

  // Notes on the sheet:
  //   INPUTS to your circuit
  //   DON'T CHANGE THE LOCATIONS OF THE INPUTS AND OUTPUTS!
  //   OUTPUT from your circuit
endmodule
