// Logisim project control_logic.circ as structural Verilog: 1 circuit, main circuit control_logic
module control_logic (
  input  [31:0] inst,
  input  BrEq,
  input  BrLt,
  output PCSel,
  output RegWEn,
  output [2:0] ImmSel,
  output BrUn,
  output ASel,
  output BSel,
  output [3:0] ALUSel,
  output MemRW,
  output [1:0] WBSel,
  output CSRSel,
  output CSRWen
);

  wire add0, alu_out, and1, and_1_out, and_2_out, and_3_out, and_4_out, and_5_out, and_6_out, and_7_out,
       and_8_out, and_9_out, and_10_out, and_11_out, and_12_out, and_13_out, and_14_out, and_15_out,
       and_16_out, and_18_out, and_19_out, and_20_out, and_21_out, and_22_out, beq_out, bge_out, bgeu_out,
       blt_out, bltu_out, bne_out, f3un0, f3un1, f3un2, f3un3, f3un4, f3un5, f3un6, f3un7, f70x00, f70x01,
       f70x20, I0x03, I0x13, I0x67, I0x73, mul10, mulh11, mulhu14, nor_1_out, or2, or_14_out, or_15_out,
       pc4_out, R0x33, SB, SB0x63, sll6, slt7, sra5, srl4, sub12, U0x17, U0x37, UJ0x6f, xor3;

  and and_1 (and_1_out, inst[6], inst[5], ~inst[4], ~inst[2], inst[1], inst[0]);  // AND_Gate
  and and_2 (and_2_out, ~inst[6], ~inst[5], inst[4], inst[2], inst[1], inst[0]);  // AND_Gate
  or or_1 (ImmSel[1], and_1_out, and_2_out, and_3_out);
  and beq (beq_out, BrEq, ~inst[14], ~inst[13], ~inst[12]);  // AND_Gate
  and and_3 (and_3_out, ~inst[6], inst[5], inst[4], inst[2], inst[1], inst[0]);  // AND_Gate
  and bne (bne_out, ~BrEq, ~inst[14], ~inst[13], inst[12]);  // AND_Gate
  and blt (blt_out, BrLt, inst[14], ~inst[13], ~inst[12]);  // AND_Gate
  and and_4 (and_4_out, R0x33, f3un0, f70x00);
  and and_5 (and_5_out, I0x13, f3un0);
  and and_6 (and_6_out, R0x33, f3un7, f70x00);
  and and_7 (and_7_out, I0x13, f3un7);
  and and_8 (and_8_out, R0x33, f3un6, f70x00);
  and and_9 (and_9_out, I0x13, f3un6);
  and and_10 (and_10_out, R0x33, f3un4, f70x00);
  and and_11 (and_11_out, I0x13, f3un4);
  and and_12 (and_12_out, R0x33, f3un5, f70x00);
  and and_13 (and_13_out, I0x13, f3un5);
  and and_14 (and_14_out, R0x33, f3un5, f70x20);
  and and_15 (and_15_out, I0x13, f3un5, f70x20);
  and and_16 (and_16_out, ~inst[6], inst[5], ~inst[4], ~inst[2], inst[1], inst[0]);  // AND_Gate
  or or_2 (ImmSel[0], and_2_out, and_3_out, and_16_out);
  and and_17 (BrUn, SB0x63, inst[13], inst[14]);
  and bge (bge_out, ~BrLt, inst[14], ~inst[13], inst[12]);  // AND_Gate
  or or_3 (add0, MemRW, and_5_out, I0x03, and_4_out, U0x17, UJ0x6f, I0x67, SB0x63);
  and bltu (bltu_out, BrLt, inst[14], inst[13], ~inst[12]);  // AND_Gate
  or or_4 (and1, and_6_out, and_7_out);
  or or_5 (or2, and_8_out, and_9_out);
  or or_6 (xor3, and_10_out, and_11_out);
  or or_7 (srl4, and_12_out, and_13_out);
  or or_8 (sra5, and_14_out, and_15_out);
  and bgeu (bgeu_out, ~BrLt, inst[14], inst[13], inst[12]);  // AND_Gate
  or or_9 (SB, bgeu_out, bltu_out, bge_out, blt_out, bne_out, beq_out);
  or pc4 (pc4_out, I0x67, UJ0x6f);
  or alu (alu_out, R0x33, I0x13);
  and and_18 (and_18_out, SB0x63, SB);
  and WBSel1 (WBSel[1], ~alu_out, ~I0x03, U0x37, pc4_out);  // AND_Gate
  or or_10 (RegWEn, R0x33, I0x13, I0x03, U0x17, U0x37, UJ0x6f, I0x67);
  and WBSel0 (WBSel[0], ~alu_out, I0x03, ~U0x37, pc4_out);  // AND_Gate
  or or_11 (PCSel, I0x67, UJ0x6f, and_18_out);
  and and_19 (and_19_out, R0x33, f3un1, f70x00);
  and and_20 (and_20_out, I0x13, f3un1, f70x00);
  and and_21 (and_21_out, R0x33, f3un2, f70x00);
  and and_22 (and_22_out, I0x13, f3un2);
  or or_12 (sll6, and_19_out, and_20_out);
  or or_13 (slt7, and_21_out, and_22_out);
  and and_23 (mul10, R0x33, f3un0, f70x01);
  and and_24 (mulh11, R0x33, f3un1, f70x01);
  and and_25 (sub12, R0x33, f3un0, f70x20);
  and and_26 (mulhu14, R0x33, f3un3, f70x01);
  Priority_Encoder #(.select(4)) priority_encoder_1 (
    .in0(add0), .in1(and1), .in2(or2), .in3(xor3), .in4(srl4), .in5(sra5), .in6(sll6), .in7(slt7),
    .in10(mul10), .in11(mulh11), .in12(sub12), .in14(mulhu14), .out(ALUSel));  // open: in8, in9, in13, in15, gs, en_out, en_in
  and and_27 (R0x33, ~inst[6], inst[5], inst[4], ~inst[3], ~inst[2], inst[1], inst[0]);  // AND_Gate
  nor nor_1 (nor_1_out, R0x33, I0x13, I0x03, MemRW, I0x67);
  and and_28 (ASel, nor_1_out, or_14_out);
  and and_29 (I0x13, ~inst[6], ~inst[5], inst[4], ~inst[3], ~inst[2], inst[1], inst[0]);  // AND_Gate
  and and_30 (I0x03, ~inst[6], ~inst[5], ~inst[4], ~inst[3], ~inst[2], inst[1], inst[0]);  // AND_Gate
  or or_14 (or_14_out, SB0x63, U0x17, UJ0x6f);
  and and_31 (MemRW, ~inst[6], inst[5], ~inst[4], ~inst[3], ~inst[2], inst[1], inst[0]);  // AND_Gate
  and and_32 (SB0x63, inst[6], inst[5], ~inst[4], ~inst[3], ~inst[2], inst[1], inst[0]);  // AND_Gate
  and and_33 (U0x17, ~inst[6], ~inst[5], inst[4], ~inst[3], inst[2], inst[1], inst[0]);  // AND_Gate
  and and_34 (U0x37, ~inst[6], inst[5], inst[4], ~inst[3], inst[2], inst[1], inst[0]);  // AND_Gate
  and and_35 (UJ0x6f, inst[6], inst[5], ~inst[4], inst[3], inst[2], inst[1], inst[0]);  // AND_Gate
  and and_36 (I0x67, inst[6], inst[5], ~inst[4], ~inst[3], inst[2], inst[1], inst[0]);  // AND_Gate
  and and_37 (I0x73, inst[6], inst[5], inst[4], ~inst[3], ~inst[2], inst[1], inst[0]);  // AND_Gate
  and f7_0 (f3un0, ~inst[14], ~inst[13], ~inst[12]);  // AND_Gate
  and f1 (f3un1, ~inst[14], ~inst[13], inst[12]);  // AND_Gate
  or or_15 (or_15_out, I0x67, UJ0x6f, U0x17, SB0x63, MemRW, I0x03, I0x13);
  and f2 (f3un2, ~inst[14], inst[13], ~inst[12]);  // AND_Gate
  and and_38 (f3un3, ~inst[14], inst[13], inst[12]);  // AND_Gate
  and and_39 (BSel, or_15_out, ~R0x33);  // AND_Gate
  and and_40 (f3un4, inst[14], ~inst[13], ~inst[12]);  // AND_Gate
  and and_41 (f3un5, inst[14], ~inst[13], inst[12]);  // AND_Gate
  and and_42 (f3un6, inst[14], inst[13], ~inst[12]);  // AND_Gate
  and and_43 (f3un7, inst[14], inst[13], inst[12]);
  and and_44 (f70x00, ~inst[31], ~inst[30], ~inst[29], ~inst[28], ~inst[27], ~inst[26], ~inst[25]);  // AND_Gate
  and and_45 (f70x01, ~inst[31], ~inst[30], ~inst[29], ~inst[28], ~inst[27], ~inst[26], inst[25]);  // AND_Gate
  and and_46 (f70x20, ~inst[31], inst[30], ~inst[29], ~inst[28], ~inst[27], ~inst[26], ~inst[25]);  // AND_Gate

  assign ImmSel[2] = inst[3];

  // Other names for the same wires on the sheet: ImmSel2 = inst[3]; OP[6:0] = inst[6:0]; func3[2:0] = inst[14:12];
  //   func7[6:0] = inst[31:25]; S0x23 = MemRW

  // Notes on the sheet:
  //   INPUTS to your circuit
  //   ImmSel
  //   DON'T CHANGE THE LOCATIONS OF THE INPUTS AND OUTPUTS!
  //   OUTPUT from your circuit
  //   WBSel
  //   PCSel
endmodule
