// Logisim project cpu.circ as structural Verilog: 1 circuit, main circuit cpu
module cpu (
  input  clk,
  input  [31:0] INSTRUCTION,
  input  [31:0] READ_DATA,
  output [31:0] WRITE_ADDRESS,
  output [31:0] PROGRAM_COUNTER,
  output [31:0] ra,
  output [31:0] sp,
  output [31:0] t0,
  output [31:0] t1,
  output [31:0] t2,
  output [31:0] s0,
  output [31:0] s1,
  output [31:0] a0,
  output [31:0] tohost,
  output [3:0] WRITE_ENABLE,
  output [31:0] WRITE_DATA
);

  wire ASel, BrEq, BrLt, BrUn, BSel, csr_1_p2, csr_1_p3, CSRSel, CSRWen, f3un0, f3un1, f3un2, f3un3, f3un4,
       f3un5, f3un6, f3un7, MemRW, PCSel, RegWEn;
  wire [1:0] WBSel;
  wire [2:0] func3, ImmSel;
  wire [3:0] ALUSel, and_6_out, and_7_out, and_8_out, bit_extender_1_out, bit_extender_2_out,
       bit_extender_3_out, bit_extender_4_out, or_1_out;
  wire [6:0] func7, OP;
  wire [24:7] PIPED_INST;
  wire [31:0] adder_1_out, and_10_out, and_11_out, and_12_out, bit_extender_5_out, bit_extender_6_out,
       bit_extender_7_out, bit_extender_8_out, bit_extender_9_out, data1, data2, imm, Mem_data,
       multiplexer_1_out, multiplexer_3_out, multiplexer_4_out, multiplexer_5_out, offset, or_2_out, PC, PC4,
       Write_Data_t;

  and f7_0 (f3un0, ~func3[2], ~func3[1], ~func3[0]);  // AND_Gate
  control_logic control_logic_1 (
    .CSRWen(CSRWen), .PCSel(PCSel), .RegWEn(RegWEn), .ImmSel(ImmSel), .BrUn(BrUn), .ASel(ASel), .BSel(BSel),
    .ALUSel(ALUSel), .MemRW(MemRW), .WBSel(WBSel), .CSRSel(CSRSel),
    .inst({func7, PIPED_INST[24:15], func3, PIPED_INST[11:7], OP}), .BrEq(BrEq), .BrLt(BrLt));
  Register #(.width(32)) register_1 (
    .D(multiplexer_1_out), .clk(clk), .Q({func7, PIPED_INST[24:15], func3, PIPED_INST[11:7], OP}));  // open: en, clr
  Multiplexer #(.enable("false"), .width(32)) multiplexer_1 (
    .in0(INSTRUCTION), .in1(32'h13), .out(multiplexer_1_out), .sel(PCSel));
  and f1 (f3un1, ~func3[2], ~func3[1], func3[0]);  // AND_Gate
  and f2 (f3un2, ~func3[2], func3[1], ~func3[0]);  // AND_Gate
  and and_1 (f3un3, ~func3[2], func3[1], func3[0]);  // AND_Gate
  and and_2 (f3un4, func3[2], ~func3[1], ~func3[0]);  // AND_Gate
  and and_3 (f3un5, func3[2], ~func3[1], func3[0]);  // AND_Gate
  and and_4 (f3un6, func3[2], func3[1], ~func3[0]);  // AND_Gate
  and and_5 (f3un7, func3[2], func3[1], func3[0]);
  regfile regfile_1 (
    .rs1(PIPED_INST[19:15]), .rs2(PIPED_INST[24:20]), .rd(PIPED_INST[11:7]), .Write_Data(Write_Data_t),
    .RegWEn(RegWEn), .clk(clk), .ra(ra), .sp(sp), .t0(t0), .t1(t1), .t2(t2), .s0(s0), .s1(s1), .a0(a0),
    .Read_Data_1(data1), .Read_Data_2(data2));
  branch_comp branch_comp_1 (.rs1(data1), .rs2(data2), .BrUn(BrUn), .BrEq(BrEq), .BrLt(BrLt));
  imm_gen imm_gen_1 (.inst({func7, PIPED_INST[24:15], func3, PIPED_INST[11:7], OP}), .ImmSel(ImmSel), .imm(imm));
  Multiplexer #(.enable("false"), .select(2), .width(32)) multiplexer_2 (
    .in0(WRITE_ADDRESS), .in1(Mem_data), .in2(offset), .in3(PC4), .out(Write_Data_t), .sel(WBSel));
  assign bit_extender_1_out = {{3{f3un0}}, f3un0};  // Bit_Extender bit_extender_1
  assign and_6_out = bit_extender_1_out & 4'b0001;  // AND_Gate and_6, 4 bits wide
  assign bit_extender_2_out = {{3{f3un1}}, f3un1};  // Bit_Extender bit_extender_2
  assign and_7_out = bit_extender_2_out & 4'b0011;  // AND_Gate and_7, 4 bits wide
  assign bit_extender_3_out = {{3{f3un2}}, f3un2};  // Bit_Extender bit_extender_3
  assign and_8_out = bit_extender_3_out & 4'b0111;  // AND_Gate and_8, 4 bits wide
  assign bit_extender_4_out = {{3{MemRW}}, MemRW};  // Bit_Extender bit_extender_4
  assign bit_extender_5_out = {{31{f3un0}}, f3un0};  // Bit_Extender bit_extender_5
  assign bit_extender_6_out = {{24{READ_DATA[7]}}, READ_DATA[7:0]};  // Bit_Extender bit_extender_6
  assign bit_extender_7_out = {{31{f3un1}}, f3un1};  // Bit_Extender bit_extender_7
  assign bit_extender_8_out = {{16{READ_DATA[15]}}, READ_DATA[15:0]};  // Bit_Extender bit_extender_8
  assign bit_extender_9_out = {{31{f3un2}}, f3un2};  // Bit_Extender bit_extender_9
  assign or_1_out = and_8_out | and_7_out | and_6_out;  // OR_Gate or_1, 4 bits wide
  assign WRITE_ENABLE = bit_extender_4_out & or_1_out;  // AND_Gate and_9, 4 bits wide
  assign and_10_out = bit_extender_5_out & bit_extender_6_out;  // AND_Gate and_10, 32 bits wide
  assign and_11_out = bit_extender_7_out & bit_extender_8_out;  // AND_Gate and_11, 32 bits wide
  assign and_12_out = bit_extender_9_out & READ_DATA;  // AND_Gate and_12, 32 bits wide
  assign or_2_out = and_12_out | and_11_out | and_10_out;  // OR_Gate or_2, 32 bits wide
  assign Mem_data = READ_DATA & or_2_out;  // AND_Gate and_13, 32 bits wide
  Adder #(.width(32)) adder_1 (.a(PROGRAM_COUNTER), .b(32'h4), .out(adder_1_out));  // open: cin, cout
  // csr csr_1: pin names not known; wires that end beside it: tohost, csr_1_p2, csr_1_p3
  Multiplexer #(.enable("false"), .width(32)) multiplexer_3 (
    .in0(adder_1_out), .in1(WRITE_ADDRESS), .out(multiplexer_3_out), .sel(PCSel));
  Register #(.width(32)) u_PC (.D(multiplexer_3_out), .clk(clk), .Q(PROGRAM_COUNTER));  // open: en, clr
  Register #(.width(32)) register_2 (.D(PROGRAM_COUNTER), .clk(clk), .Q(PC));  // open: en, clr
  Multiplexer #(.enable("false"), .width(32)) multiplexer_4 (
    .in0(data1), .in1(PC), .out(multiplexer_4_out), .sel(ASel));
  Multiplexer #(.enable("false"), .width(32)) multiplexer_5 (
    .in0(data2), .in1(imm), .out(multiplexer_5_out), .sel(BSel));
  alu alu_1 (.Result(WRITE_ADDRESS), .A(multiplexer_4_out), .B(multiplexer_5_out), .ALUSel(ALUSel));
  Adder #(.width(32)) adder_2 (.a(32'h4), .b(PC), .out(PC4));  // open: cin, cout

  // Other names for the same wires on the sheet: ALURes[31:0] = WRITE_ADDRESS;
  //   PIPED_INST (some bits) = {func7, func3, OP}; rd[4:0] = PIPED_INST[11:7]; rs1[4:0] = PIPED_INST[19:15];
  //   rs2[4:0] = PIPED_INST[24:20]

  // Notes on the sheet:
  //   Output to IMEM
  //   IMEM (do **NOT** move this)
  //   Inputs from IMEM
  //   It is OK to move the PC, RegFile, ALU, MEM, Branch Comp, Imm Gen, and Control Logic to wherever is most convenient for you when constructing your CPU, and to delete this text
  //   Inputs/Outputs for testing. Do **NOT** move these.
  //   Outputs To DMEM
  //   DMEM (do **NOT** move this)
  //   Inputs From DMEM
endmodule
